# Fritzing sketch esquema-electrico (saved by Fritzing 0.9.3b)
breadboards: 1

parts:
  R1 = Resistor [tolerance=±5% resistance=220 package=THT]
  LED1 = LED - 5mm [color="Red (633nm)" package="5 mm [THT]"]

nets:
  GND: R1.Pin_0
  N1: R1.Pin_1, LED1.cathode
  5V: LED1.anode
