# Fritzing sketch fritzing (saved by Fritzing 0.8.7b)
breadboards: 1

parts:
  R1 = Resistor [tolerance=±5% resistance=220 package=THT]
  LED1 = LED - 5mm [color="Blue (430nm)" package="5 mm [THT]"]
  LED3 = LED - 5mm [color="White (8000K)" package="5 mm [THT]"]
  R2 = Photocell (LDR) [package=THT]
  RHT1 = Humidity and Temperature Sensor RHT03
  LED4 = LED - 5mm [color="Red (633nm)" package="5 mm [THT]"]
  R3 = Resistor [tolerance=±5% resistance=220 package=THT]
  R4 = Resistor [tolerance=±5% resistance=1k package=THT]
  R5 = Resistor [tolerance=±5% resistance=220 package=THT]
  Parte1 = Arduino Uno (Rev3)
  T1 = LM35 Temperature Sensor [package="TO92 [THT]"]

nets:
  N1: R1.Pin_0, LED3.cathode
  N2: R1.Pin_1, RHT1.GND_1, RHT1.GND_2, R3.Pin_1, R4.Pin_1, R5.Pin_1, Parte1.GND, T1.Vout
  N3: LED1.cathode, R5.Pin_0
  N4: LED1.anode, Parte1.D11_PWM/MOSI
  N5: LED3.anode, Parte1.D12/MISO
  N6: R2.pin_0, R4.Pin_0, Parte1.A1
  VCC: R2.pin_1, RHT1.Vcc, Parte1.5V, T1.+Vs
  N7: RHT1.Data-signal, Parte1.A0
  N8: LED4.cathode, R3.Pin_0
  N9: LED4.anode, Parte1.D13/SCK
  N10: Parte1.A2, T1.GND
