# Fritzing sketch fritzing (saved by Fritzing 0.9.3b)
breadboards: 1

parts:
  U1 = NodeMCU V1.0
  R1 = Resistor [tolerance=±5% resistance=330k package=THT]
  LED1 = LED - 5mm [color="Red (633nm)" package="5 mm [THT]"]

nets:
  N1: U1.GND, LED1.cathode
  N2: U1.D5, R1.Pin_1
  N3: R1.Pin_0, LED1.anode

custom parts:
  NodeMCU V1.0: ESP8266 based NodeMCU
